# Fritzing sketch Hexapod Planning (saved by Fritzing 0.9.2b)

parts:
  BeagleBone1 = BeagleBone Black
  Part1 = 16-Channel 12-bit PCA9685 PWM/Servo Driver
  Part2 = 16-Channel 12-bit PCA9685 PWM/Servo Driver
  SERVO1 = Adafruit Feedback Servo (small)
  SERVO2 = Adafruit Feedback Servo (small)
  SERVO3 = Adafruit Feedback Servo (small)
  SERVO4 = Adafruit Feedback Servo (small)
  SERVO5 = Adafruit Feedback Servo (small)
  SERVO6 = Adafruit Feedback Servo (small)
  SERVO7 = Adafruit Feedback Servo (small)
  SERVO8 = Adafruit Feedback Servo (small)
  SERVO9 = Adafruit Feedback Servo (small)
  Part3 = 9-DOF Absolute Orientation IMU Fusion Breakout - BNO055
  OLED2 = 1.27" 128x96 16-bit OLED Breakout  # not connected
  SW1 = ENCODER_RGB_CA [package=encoder_led_3]  # not connected
  SERVO10 = Adafruit Feedback Servo (small)  # not connected
  SERVO11 = Adafruit Feedback Servo (small)  # not connected
  SERVO13 = Adafruit Feedback Servo (small)  # not connected
  SERVO14 = Adafruit Feedback Servo (small)  # not connected
  SERVO17 = Adafruit Feedback Servo (small)  # not connected
  SERVO18 = Adafruit Feedback Servo (small)  # not connected
  SERVO19 = Adafruit Feedback Servo (small)  # not connected
  SERVO20 = Adafruit Feedback Servo (small)  # not connected
  SERVO21 = Adafruit Feedback Servo (small)  # not connected
  J2 = Basic Force Sensing Resistor (FSR) [package=THT]  # not connected
  J4 = Basic Force Sensing Resistor (FSR) [package=THT]  # not connected
  J3 = Basic Force Sensing Resistor (FSR) [package=THT]  # not connected
  J5 = Basic Force Sensing Resistor (FSR) [package=THT]  # not connected
  J6 = Basic Force Sensing Resistor (FSR) [package=THT]  # not connected
  J1 = Basic Force Sensing Resistor (FSR) [package=THT]
  Part4 = Analog Digital MUX Breakout
  VCC1 = 4 x AAA Battery Mount

nets:
  GND: BeagleBone1.no_name_yet#1, Part1.GND, Part2.GND, SERVO1.Ground, SERVO2.Ground, SERVO3.Ground, SERVO4.Ground, SERVO5.Ground, SERVO6.Ground, SERVO7.Ground, SERVO8.Ground, SERVO9.Ground, J1.pin_1, Part4.GND, Part4.EN, Part4.S2, Part4.S3, VCC1.-
  VCC: BeagleBone1.no_name_yet#3, Part1.VCC, Part2.VCC, Part2.A0
  N1: BeagleBone1.no_name_yet#4, Part3.5.0V
  N2: BeagleBone1.no_name_yet#5, Part4.VCC
  N3: BeagleBone1.no_name_yet#10, Part3.RST_5V
  N4: BeagleBone1.no_name_yet#19, Part1.SCL, Part2.SCL
  N5: BeagleBone1.no_name_yet#20, Part1.SDA, Part2.SDA
  N6: BeagleBone1.no_name_yet#21, Part3.SCL_5V
  N7: BeagleBone1.no_name_yet#22, Part3.SDA_5V
  N8: BeagleBone1.no_name_yet#36, Part4.SIG
  N9: BeagleBone1.no_name_yet#45, Part3.GND
  N10: BeagleBone1.no_name_yet#113, Part4.S0
  N11: BeagleBone1.no_name_yet#114, Part4.S1
  N12: Part1.PWRIN, VCC1.+
  N13: Part1.0, SERVO9.Signal
  N14: Part1.1, SERVO8.Signal
  N15: Part1.V+, Part2.V+, SERVO1.Power, SERVO2.Power, SERVO3.Power, SERVO4.Power, SERVO5.Power, SERVO6.Power, SERVO7.Power, SERVO8.Power, SERVO9.Power
  N16: Part1.2, SERVO7.Signal
  N17: Part1.4, SERVO6.Signal
  N18: Part1.5, SERVO5.Signal
  N19: Part1.6, SERVO4.Signal
  N20: Part1.OE, Part2.OE
  N21: Part1.8, SERVO3.Signal
  N22: Part1.9, SERVO2.Signal
  N23: Part1.10, SERVO1.Signal
  N24: SERVO7.Feedback, Part4.C0
  N25: SERVO8.Feedback, Part4.C1
  N26: SERVO9.Feedback, Part4.C2
  N27: J1.pin_0, Part4.C3

custom parts:
  BeagleBone Black: BeagleBone Black rev. A5B
  16-Channel 12-bit PCA9685 PWM/Servo Driver: The Adafruit 16-Channel 12-bit PWM/Servo Driver will drive up to 16 servos over I2C with only 2 pins. The on-board PCA9685 PWM controller will drive all 16 channels simultaneously with no additional processing overhead. What's more, you can chain up to 62 of them to control up to 992 servos - all with the same 2 pins
  Adafruit Feedback Servo (small): Adafruit Feedback Servo (Small)
  9-DOF Absolute Orientation IMU Fusion Breakout - BNO055: A MEMS accelerometer, magnetometer and gyroscope on a single die with a high speed ARM Cortex-M0 based processor to digest all the sensor data, abstract the sensor fusion and real time requirements away, and spit out data you can use in quaternions, Euler angles or vectors.
