# Fritzing sketch Hexapod Single Leg (saved by Fritzing 0.9.2b)

parts:
  Part1 = Analog Digital MUX Breakout
  J1 = Basic Force Sensing Resistor (FSR) [package=THT]
  Part3 = 16-Channel 12-bit PCA9685 PWM/Servo Driver
  SERVO1 = Adafruit Feedback Servo (large)
  SERVO2 = Adafruit Feedback Servo (large)
  SERVO3 = Adafruit Feedback Servo (large)
  R1 = Resistor [tolerance=±5% resistance=10k package=THT]

nets:
  N1: Part1.C0, SERVO2.Feedback
  N2: Part1.C1, SERVO3.Feedback
  N3: Part1.C2, SERVO1.Feedback
  N4: Part1.C3, J1.pin_0, R1.Pin_1
  GND: Part1.GND, Part3.GND, SERVO1.Ground, SERVO2.Ground, SERVO3.Ground, R1.Pin_0
  N5: Part1.VCC, J1.pin_1, Part3.V+, SERVO1.Power, SERVO2.Power, SERVO3.Power
  N6: Part3.4, SERVO1.Signal
  N7: Part3.5, SERVO3.Signal
  N8: Part3.6, SERVO2.Signal

custom parts:
  16-Channel 12-bit PCA9685 PWM/Servo Driver: The Adafruit 16-Channel 12-bit PWM/Servo Driver will drive up to 16 servos over I2C with only 2 pins. The on-board PCA9685 PWM controller will drive all 16 channels simultaneously with no additional processing overhead. What's more, you can chain up to 62 of them to control up to 992 servos - all with the same 2 pins
  Adafruit Feedback Servo (large): Adafruit Feedback Servo (Small)
